# Fritzing sketch prototype_schematic (saved by Fritzing 0.9.9b)
breadboards: 1

parts:
  R1 = Resistor [tolerance=±5% power=0.25 resistance=4.7k package=THT]
  S1 = Round Pushbutton
  VCC1 = 4 x AAA Battery Mount
  MCU = Arduino Uno (Rev3) - ICSP
  LED1 = Super Flux RGB LED (com. cathode)
  R2 = Resistor [tolerance=±5% power=0.25 resistance=4.7k package=THT]
  S2 = Round Pushbutton

nets:
  N1: R1.Pin_0, S1.leg0, MCU.D2
  N2: R1.Pin_1, VCC1.-, MCU.GND, LED1.common_cathode, R2.Pin_1
  N3: S1.leg1, MCU.5V, S2.leg1
  N4: VCC1.+, MCU.VIN
  N5: MCU.D3_PWM, R2.Pin_0, S2.leg0
  N6: MCU.D4, LED1.red_anode
  N7: MCU.D5_PWM, LED1.green_anode
  N8: MCU.D6_PWM, LED1.blue_anode
