# Fritzing sketch test_schematic (saved by Fritzing 0.9.9b)
breadboards: 1

parts:
  VCC1 = 4 x AAA Battery Mount
  MCU = Arduino Uno (Rev3) - ICSP
  LED1 = Super Flux RGB LED (com. cathode)

nets:
  N1: VCC1.-, MCU.GND, LED1.common_cathode
  N2: VCC1.+, MCU.VIN
  N3: MCU.ICSP_MOSI, MCU.D11_PWM/MOSI, MCU.D6_PWM, LED1.blue_anode
  N4: MCU.D9_PWM, MCU.D4, LED1.red_anode
  N5: MCU.D10_PWM/SS, MCU.D5_PWM, LED1.green_anode
